# Fritzing sketch foerdfunk_iot_board (saved by Fritzing 0.9.2b)
breadboards: 1

parts:
  Raspberry_Pi1 = Raspberry Pi 2
  J1 = Basic Servo
  J2 = Basic Servo
  LED1 = RGB LED (com. cathode, rgb) [package="5 mm [THT]"]

nets:
  N1: Raspberry_Pi1.GPIO21, LED1.blue_anode
  N2: Raspberry_Pi1.GPIO20, LED1.common_cathode
  N3: Raspberry_Pi1.GPIO16, LED1.red_anode
  GND: Raspberry_Pi1.GND, J1.gnd, J2.gnd
  VCC: Raspberry_Pi1.5V, J1.vcc, J2.vcc, LED1.green_anode
